# Fritzing sketch arduino-hcsr04 (saved by Fritzing 0.9.10b)

parts:
  BT1 = Bluetooth HC-06u [package=THT]
  Parça1 = Arduino Uno (Rev3)

nets:
  VCC: BT1.VCC, Parça1.5V
  GND: BT1.GND, Parça1.GND
  N1: BT1.TXD, Parça1.D5_PWM
  N2: BT1.RXD, Parça1.D6_PWM

custom parts:
  Bluetooth HC-06u: Bluetooth HC-06 - face up, pins down 16.5mm x 37.5mm PCB
