# Fritzing sketch hcsr-04 (saved by Fritzing 0.9.10b)

parts:
  BT1 = Bluetooth HC-06u [package=THT]
  Parça1 = Arduino Uno (Rev3)
  M1 = DC Mini Metal Gear Motor
  L298N1 = L298N DC motor driver
  M2 = DC Mini Metal Gear Motor
  M3 = DC Mini Metal Gear Motor
  M4 = DC Mini Metal Gear Motor
  Parça2 = SRF05 Ultrasonic Rangefinder

nets:
  VCC: BT1.VCC, Parça1.5V, Parça2.VCC
  GND: BT1.GND, Parça1.GND, Parça2.GND
  N1: BT1.TXD, Parça1.D0/RX
  N2: BT1.RXD, Parça1.D1/TX
  N3: Parça1.D9_PWM, Parça2.Trig
  N4: Parça1.D10_PWM/SS, L298N1.ENB
  N5: Parça1.D11_PWM/MOSI, L298N1.ENA
  N6: Parça1.D2, L298N1.IN1
  N7: Parça1.D3_PWM, L298N1.IN2
  N8: Parça1.D4, L298N1.IN3
  N9: Parça1.D5_PWM, L298N1.IN4
  N10: Parça1.D6_PWM, Parça2.Echo
  N11: M1.IN1, L298N1.OUT2, M2.IN1
  N12: M1.IN2, L298N1.OUT1, M2.IN2
  N13: L298N1.OUT3, M3.IN2, M4.IN2
  N14: L298N1.OUT4, M3.IN1, M4.IN1

custom parts:
  Bluetooth HC-06u: Bluetooth HC-06 - face up, pins down 16.5mm x 37.5mm PCB
  L298N DC motor driver: 2x DC motor driver with 78M05 positive voltage regulator (7..35 V) L298N: max 46 V, 2 A Set 5 V Enable jumper to enable 5 V regultor (needed for the L298N) and +5 V output at screw terminal or supply external +5 V at screw terminal Set ENA and/or ENB to +5 V to enable motor permanently or supply ENA and/or ENB with PWM signal IN1 and IN2 set rotation directory for motor A (OUT1/OUT2) IN2 and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
